# Fritzing sketch mosquito repeller (saved by Fritzing 0.9.6b)
circuit board: 8.46667cm x 5.64444cm

parts:
  U1 = 555 Timer [package="DIP8 [THT]"]
  R1 = Resistor [tolerance=±5% resistance=1k package="0402 [SMD]"]
  R2 = Resistor [tolerance=±5% resistance=1m package="0402 [SMD]"]
  XTAL1 = Crystal [frequency="16 Mhz" package=THT]
  C3 = Capacitor [package=cap-pth-small-kit]
  C4 = Capacitor [package=cap-pth-small-kit]

nets:
  N1: U1.Ground, C3.2, C4.2
  N2: U1.Trigger, U1.Threshold, U1.Discharge, R1.Pin_1, R2.Pin_0, R2.Pin_1, C3.1
  N3: U1.Output, XTAL1.pin_0
  N4: U1.Reset, XTAL1.pin_1
  N5: U1.Control_Voltage, C4.1
  N6: U1.Vcc_Supply_Voltage, R1.Pin_0
